# Fritzing sketch pomodoro (saved by Fritzing 0.5.2b)
breadboards: 1

parts:
  Arduino1 = Arduino
  LED1 = Red LED - 5mm [package="5 mm [THT]"]
  LED2 = green LED - 5mm [package="5 mm [THT]"]
  R1 = Resistor [resistance=330 package=THT]
  R1_2 = Resistor [resistance=330 package=THT]
  R1_3 = Resistor [resistance=330 package=THT]
  R1_4 = Resistor [resistance=330 package=THT]
  R1_5 = Resistor [resistance=330 package=THT]
  LED2_2 = green LED - 5mm [package="5 mm [THT]"]
  LED2_3 = green LED - 5mm [package="5 mm [THT]"]
  LED2_4 = green LED - 5mm [package="5 mm [THT]"]
  J1 = Basic Servo
  J2 = Piezo Speaker
  R1_6 = Resistor [resistance=330 package=THT]
  R1_7 = Resistor [resistance=10k package=THT]
  S1 = Pushbutton [package="[THT]"]

nets:
  GND: Arduino1.GND, LED1.cathode, LED2.cathode, R1_5.Pin_0, LED2_2.cathode, LED2_3.cathode, LED2_4.cathode, LED2_4.anode, J1.gnd, J2.pin2, S1.Pin_1, S1.Pin_2
  N1: Arduino1.D13, R1_6.Pin_1
  N2: Arduino1.D11, J1.pulse
  N3: Arduino1.D10, R1_4.Pin_1
  N4: Arduino1.D9, R1_5.Pin_1
  N5: Arduino1.D6, R1_3.Pin_1
  N6: Arduino1.D5, R1_2.Pin_1
  N7: Arduino1.D3, R1.Pin_1
  N8: Arduino1.RST, R1_7.Pin_1, S1.Pin_3, S1.Pin_4
  +5V: Arduino1.+5V, J1.vcc, R1_7.Pin_0
  N9: LED1.anode, R1_4.Pin_0
  N10: LED2.anode, R1.Pin_0
  N11: R1_2.Pin_0, LED2_2.anode
  N12: R1_3.Pin_0, LED2_3.anode
  N13: J2.pin1, R1_6.Pin_0
